# Fritzing sketch AutoTurntable (saved by Fritzing 0.9.9b)
breadboards: 2

parts:
  A1 = Arduino Nano (Rev3.0)
  U1 = MUX36S16DA [chip_label=MUX36S16DA package="DIP (Dual Inline) [THT]"]
  J3 = shrouded pin header, 6 pins [form="♂ (shrouded male)"]
  J1 = Screw terminal - 2 pins [package=THT]
  J2 = shrouded pin header, 6 pins [form="♂ (shrouded male)"]
  JP1 = male pin header, 3 pins [form="♂ (male)"]
  J5 = shrouded pin header, 6 pins [form="♂ (shrouded male)"]
  C1 = Electrolytic Capacitor [capacitance=3.3µF voltage=50V package="100 mil [THT, electrolytic]"]
  J9 = shrouded pin header, 6 pins [form="♂ (shrouded male)"]
  R4 = Resistor [tolerance=±5% power=0.25 resistance=1k package=THT]
  J4 = shrouded pin header, 8 pins [form="♂ (shrouded male)"]
  R5 = Resistor [tolerance=±5% power=0.25 resistance=1k package=THT]
  R6 = Resistor [tolerance=±5% power=0.25 resistance=1k package=THT]
  R7 = Resistor [tolerance=±5% power=0.25 resistance=1k package=THT]
  D1 = Rectifier Diode [part_number=1N007 package="300 mil [THT]"]
  U2 = ADG333AB [chip_label=U package="DIP (Dual Inline) [THT]"]
  R8 = Resistor [tolerance=±5% power=0.25 resistance=1k package=THT]
  J6 = female pin header, 2 pins [form="♀ (female)"]
  Q2 = Basic FET P-Channel [part_number=TIP120 package="TO220 [THT]"]
  U3 = ULN2003A [package="DIP16 [THT]"]
  U4 = ULN2003A [package="DIP16 [THT]"]
  C2 = Tantalum Capacitor [capacitance=20nF voltage=35V package="C 6032 [SMD, tantalum]"]
  J10 = female pin header, 5 pins [form="♀ (female)"]
  J11 = female pin header, 5 pins [form="♀ (female)"]
  JP1_2 = Header 3 [package=molex-1x3_lock]
  JP2 = Header 3 [package=molex-1x3_lock]
  JP3 = Header 3 [package=molex-1x3_lock]
  R9 = Resistor [tolerance=±5% power=0.25 resistance=10k package=THT]
  R10 = Resistor [tolerance=±5% power=0.25 resistance=10k package=THT]
  R11 = Resistor [tolerance=±5% power=0.25 resistance=10k package=THT]
  R12 = Resistor [tolerance=±5% power=0.25 resistance=10k package=THT]
  JP4 = Header 3 [package=molex-1x3_lock]
  JP5 = Header 3 [package=molex-1x3_lock]
  JP6 = Header 3 [package=molex-1x3_lock]
  JP7 = Header 3 [package=molex-1x3_lock]
  JP8 = Header 3 [package=molex-1x3_lock]
  JP9 = Header 3 [package=molex-1x3_lock]
  JP10 = Header 3 [package=molex-1x3_lock]
  J12 = female pin header, 3 pins [form="♀ (female)"]
  J15 = female pin header, 3 pins [form="♀ (female)"]
  J13 = female pin header, 3 pins [form="♀ (female)"]
  R13 = Resistor [tolerance=±5% power=0.25 resistance=10k package=THT]
  R14 = Resistor [tolerance=±5% power=0.25 resistance=10k package=THT]
  R15 = Resistor [tolerance=±5% power=0.25 resistance=10k package=THT]
  U5 = POT [package=pot_alpha_rv16af-20]
  U6 = POT [package=pot_alpha_rv16af-20]
  U7 = POT [package=pot_alpha_rv16af-20]
  U8 = POT [package=pot_alpha_rv16af-20]
  U9 = POT [package=pot_alpha_rv16af-20]
  R16 = Resistor [tolerance=±5% power=0.25 resistance=10k package=THT]
  R17 = Resistor [tolerance=±5% power=0.25 resistance=10k package=THT]
  R18 = Resistor [tolerance=±5% power=0.25 resistance=10k package=THT]
  R19 = Resistor [tolerance=±5% power=0.25 resistance=10k package=THT]
  R20 = Resistor [tolerance=±5% power=0.25 resistance=10k package=THT]
  J16 = female pin header, 5 pins [form="♀ (female)"]
  JP11 = Header 3 [package=molex-1x3_lock]
  JP12 = Header 3 [package=molex-1x3_lock]
  R21 = Resistor [tolerance=±5% power=0.25 resistance=10k package=THT]
  R22 = Resistor [tolerance=±5% power=0.25 resistance=10k package=THT]
  Q3 = Basic FET P-Channel [part_number=TIP120 package="TO220 [THT]"]
  JP13 = Header 3 [package=molex-1x3_lock]
  D2 = Rectifier Diode [part_number=1N007 package="300 mil [THT]"]
  R23 = Resistor [tolerance=±5% power=0.25 resistance=1k package=THT]
  J14 = female pin header, 3 pins [form="♀ (female)"]

nets:
  GND: A1.GND, U1.GND, U1.VSS, J1.pin2, C1.-, J9.pin6, R4.Pin_1, R5.Pin_1, R6.Pin_1, R7.Pin_1, U2.VSS, U2.GND, Q2.source, U3.0V, U4.0V, C2.+, R9.Pin_1, R10.Pin_1, R11.Pin_1, R12.Pin_1, JP5.3, JP6.3, JP7.3, JP8.3, JP9.3, JP10.3, R13.Pin_0, R14.Pin_0, R15.Pin_0, R16.Pin_0, R17.Pin_0, R18.Pin_0, R19.Pin_0, R20.Pin_0, R21.Pin_0, R22.Pin_0, Q3.source, JP13.3, J14.pin1, J14.pin2, J14.pin3
  N1: A1.D2, U1.A0
  N2: A1.D3, U1.A1
  N3: A1.D4, U1.A2
  N4: A1.D5, U1.A3
  N5: A1.D6, U1.D
  N6: A1.D7, U2.D1
  N7: A1.D8, U2.D2
  N8: A1.D9, U2.D3
  N9: A1.D10, U2.D4
  N10: A1.D11/MOSI, U2.IN1, U2.IN2, U2.IN3, U2.IN4
  N11: A1.D12/MISO, J4.pin4
  VDD: A1.VIN, U1.VDD, U1.EN, J3.pin1, J3.pin3, J2.pin5, JP1.pin2, J5.pin2, C1.+, J9.pin1, J4.pin1, D1.cathode, U2.VDD, J6.pin1, U3.COM_-_Common, U4.COM_-_Common, C2.-, J10.pin1, J11.pin1, JP1_2.1, JP2.1, JP3.1, JP4.1, JP5.2, JP6.2, JP7.2, JP8.2, JP9.2, JP10.2, J13.pin1, J13.pin2, J13.pin3, U5.S, U6.S, U7.S, U8.S, U9.S, JP11.2, JP12.2, JP13.2
  N12: A1.A7, R8.Pin_0
  N13: A1.A6, U8.A
  N14: A1.A5, J9.pin2
  N15: A1.A4, J9.pin3
  N16: A1.A3, U7.A
  N17: A1.A2, U6.A
  N18: A1.A1, U5.A
  N19: A1.A0, U9.A
  N20: A1.3V3, J15.pin1, J15.pin2, J15.pin3
  N21: A1.D13/SCK, J4.pin3
  N22: U1.S16, J12.pin1
  N23: U1.S15, J12.pin2
  N24: U1.S14, J12.pin3
  N25: U1.S13, JP10.1
  N26: U1.S12, J3.pin6, R15.Pin_1
  N27: U1.S11, JP9.1
  N28: U1.S10, J2.pin4, JP1.pin3, R14.Pin_1
  N29: U1.S9, J2.pin6, JP1.pin1, R13.Pin_1
  N30: U1.S1, R9.Pin_0, JP4.3
  N31: U1.S2, JP3.3, R10.Pin_0
  N32: U1.S3, JP1_2.3, R11.Pin_0
  N33: U1.S4, JP2.3, R12.Pin_0
  N34: U1.S5, JP8.1
  N35: U1.S6, JP5.1
  N36: U1.S7, JP6.1
  N37: U1.S8, JP7.1
  N38: J3.pin2, J3.pin5, J1.pin1
  N39: J5.pin1, J5.pin3, J4.pin2
  N40: J5.pin4, JP12.1
  N41: J5.pin5, J16.pin2, D2.cathode
  N42: J5.pin6, JP11.1
  N43: R4.Pin_0, J4.pin5
  N44: J4.pin6, R5.Pin_0
  N45: J4.pin7, R6.Pin_0
  N46: J4.pin8, R7.Pin_0
  N47: D1.anode, J6.pin2, Q2.drain
  N48: U2.S1A, U4.In_1
  N49: U2.S1B, U3.In_1
  N50: U2.S2B, U3.In_2
  N51: U2.S2A, U4.In_2
  N52: U2.S3A, U4.In_3
  N53: U2.S3B, U3.In_3
  N54: U2.S4B, U3.In_4
  N55: U2.S4A, U4.In_4
  N56: R8.Pin_1, Q2.gate
  N57: U3.Out_4, J11.pin5
  N58: U3.Out_3, J11.pin4
  N59: U3.Out_2, J11.pin3
  N60: U3.Out_1, J11.pin2
  N61: U4.Out_4, J10.pin5
  N62: U4.Out_3, J10.pin4
  N63: U4.Out_2, J10.pin3
  N64: U4.Out_1, J10.pin2
  N65: U5.E, R19.Pin_1
  N66: U6.E, R18.Pin_1
  N67: U7.E, R17.Pin_1
  N68: U8.E, R16.Pin_1
  N69: U9.E, R20.Pin_1
  N70: J16.pin1, Q3.drain, D2.anode
  N71: J16.pin3, J16.pin4
  N72: JP11.3, R21.Pin_1
  N73: JP12.3, R22.Pin_1
  N74: Q3.gate, R23.Pin_1
  N75: JP13.1, R23.Pin_0

notes:
  Power SW
  DC in
  Speed SW
  Size SW
  Size Jumper
  12" Play Sensor
  LEDs
  PW SW
  SP SW
  SZ SW
  7-Seg Disp.
  Solenoid
  7S SP
  SOl
  7"
  12"
  NC = 10"
  Designed by Patrick Nelson (2021)
  Vertical Motor
  Horiz. Motor
  [
  Upper Limit
  Lower Limit
  V MTR
  H MTR
  Pause Button
  Play/Home Button
  U LIM
  L LIM
  PAUS BTN
  PLY BTN
  7" Play Sensor
  10" Play Sensor
  Home Sensor
  7" SEN
  10" SEN
  12" SEN
  HOME SEN
  Pickup Sensor
  Speed Sensor
  Unused Mux Pins
  5v DC
  3.3v DC
  GND
  SPD SEN
  PKU SEN
  Mux In
  S14
  S15
  S16
  7" Cal Pot
  10" Cal Pot
  12" Cal Pot
  Home Cal Pot
  Pickup Del Pot
  5v DC In
  +
  -
  33-RPM Pot
  45-RPM Pot
  Turntable power sensor
  33-RPM POT
  45-RPM POT
  TURN ON-OFF
  TURN MTR

custom parts:
  MUX36S16DA: A DIP stand-in part for whatever IC you want. With 28 pins on a 600mil dual inline package (DIP) footprint.
  ADG333AB: A DIP stand-in part for whatever IC you want. With 20 pins on a 300mil dual inline package (DIP) footprint.
