# Fritzing sketch AutoTurntable (saved by Fritzing 0.9.9b)
circuit board: 11cm x 17cm
breadboards: 3

parts:
  A1 = Arduino Nano (Rev3.0)
  J6 = shrouded pin header, 6 pins [form="♂ (shrouded male)"]
  J12 = shrouded pin header, 6 pins [form="♂ (shrouded male)"]
  JP1 = male pin header, 3 pins [form="♂ (male)"]
  J7 = shrouded pin header, 6 pins [form="♂ (shrouded male)"]
  C1 = Electrolytic Capacitor [capacitance=3.3µF voltage=50V package="100 mil [THT, electrolytic]"]
  J11 = shrouded pin header, 8 pins [form="♂ (shrouded male)"]
  D1 = Rectifier Diode [part_number=1N007 package="300 mil [THT]"]
  Q1 = Basic FET P-Channel [part_number=TIP120 package="TO220 [THT]"]
  U3 = ULN2003A [package="DIP16 [THT]"]
  U4 = ULN2003A [package="DIP16 [THT]"]
  P2 = POT [package=pot_alpha_rv16af-20]
  P3 = POT [package=pot_alpha_rv16af-20]
  P1 = POT [package=pot_alpha_rv16af-20]
  U1 = IC, DIP package, 28 pins [chip_label=IC]
  J5 = male pin header, 4 pins [form="♂ (male)"]
  J3 = male pin header, 3 pins [form="♂ (male)"]
  J4 = male pin header, 3 pins [form="♂ (male)"]
  J2 = male pin header, 3 pins [form="♂ (male)"]
  J14 = male pin header, 5 pins [form="♂ (male)"]
  J13 = male pin header, 5 pins [form="♂ (male)"]
  J21 = male pin header, 3 pins [form="♂ (male)"]
  J22 = male pin header, 3 pins [form="♂ (male)"]
  J23 = male pin header, 3 pins [form="♂ (male)"]
  J24 = male pin header, 3 pins [form="♂ (male)"]
  J25 = male pin header, 3 pins [form="♂ (male)"]
  J26 = male pin header, 3 pins [form="♂ (male)"]
  J27 = shrouded pin header, 16 pins [form="♂ (shrouded male)"]
  D3 = Rectifier Diode [part_number=1N007 package="300 mil [THT]"]
  D4 = Rectifier Diode [part_number=1N007 package="300 mil [THT]"]
  D6 = Rectifier Diode [part_number=1N007 package="300 mil [THT]"]
  J16 = male pin header, 2 pins [form="♂ (male)"]
  J1 = screw terminal, 2 pins
  U7 = Voltage Regulator - Variable [package="TO220 [THT]"]
  Q2 = Basic FET P-Channel [part_number=TIP120 package="TO220 [THT]"]
  J10 = male pin header, 5 pins [form="♂ (male)"]
  J8 = male pin header, 3 pins [form="♂ (male)"]
  J9 = male pin header, 3 pins [form="♂ (male)"]
  D12 = Rectifier Diode [part_number=1N007 package="300 mil [THT]"]
  RL1 = DPDT Relay [chip_label=Relay package="DIP (Dual Inline) [THT]"]
  D2 = Rectifier Diode [part_number=1N007 package="300 mil [THT]"]
  Q3 = Basic FET P-Channel [part_number=TIP120 package="TO220 [THT]"]
  D9 = Rectifier Diode [part_number=1N007 package="300 mil [THT]"]
  D10 = Rectifier Diode [part_number=1N007 package="300 mil [THT]"]
  D7 = Rectifier Diode [part_number=1N007 package="300 mil [THT]"]
  D8 = Rectifier Diode [part_number=1N007 package="300 mil [THT]"]
  D5 = Rectifier Diode [part_number=1N007 package="300 mil [THT]"]
  R24 = Resistor [tolerance=±5% resistance=10k power=0.25 package="0603 [SMD]"]
  R18 = Resistor [tolerance=±5% resistance=10k power=0.25 package="0603 [SMD]"]
  R19 = Resistor [tolerance=±5% resistance=10k power=0.25 package="0603 [SMD]"]
  R20 = Resistor [tolerance=±5% resistance=10k power=0.25 package="0603 [SMD]"]
  R10 = Resistor [tolerance=±5% resistance=10k power=0.25 package="0603 [SMD]"]
  R12 = Resistor [tolerance=±5% resistance=10k power=0.25 package="0603 [SMD]"]
  R11 = Resistor [tolerance=±5% resistance=10k power=0.25 package="0603 [SMD]"]
  R9 = Resistor [tolerance=±5% resistance=10k power=0.25 package="0603 [SMD]"]
  C6 = Ceramic Capacitor [capacitance="100 nF" voltage=35V package="0603 [SMD, multilayer]"]
  C3 = Ceramic Capacitor [capacitance="100 nF" voltage=35V package="0603 [SMD, multilayer]"]
  C4 = Ceramic Capacitor [capacitance="100 nF" voltage=35V package="0603 [SMD, multilayer]"]
  R15 = Resistor [tolerance=±5% resistance=10k power=0.25 package="0603 [SMD]"]
  R4 = Resistor [tolerance=±5% resistance=10k power=0.25 package="0603 [SMD]"]
  R5 = Resistor [tolerance=±5% resistance=10k power=0.25 package="0603 [SMD]"]
  R7 = Resistor [tolerance=±5% resistance=10k power=0.25 package="0603 [SMD]"]
  R13 = Resistor [tolerance=±5% resistance=10k power=0.25 package="0603 [SMD]"]
  R14 = Resistor [tolerance=±5% resistance=10k power=0.25 package="0603 [SMD]"]
  C9 = Ceramic Capacitor [capacitance="100 nF" voltage=35V package="0603 [SMD, multilayer]"]
  C8 = Ceramic Capacitor [capacitance="100 nF" voltage=35V package="0603 [SMD, multilayer]"]
  R23 = Resistor [tolerance=±5% resistance=1k power=0.25 package="0603 [SMD]"]
  R8 = Resistor [tolerance=±5% resistance=1k power=0.25 package="0603 [SMD]"]
  U8 = 74AHC1G08 [package=sot23-5]
  C13 = Ceramic Capacitor [capacitance="100 nF" voltage=35V package="0603 [SMD, multilayer]"]
  U5 = TC7SU04F [package=sot23-5]
  C11 = Ceramic Capacitor [capacitance="100 nF" voltage=35V package="0603 [SMD, multilayer]"]
  R28 = Resistor [tolerance=±5% resistance=1k power=0.25 package="0603 [SMD]"]
  R27 = Resistor [tolerance=±5% resistance=10k power=0.25 package="0603 [SMD]"]
  R26 = Resistor [tolerance=±5% resistance=10k power=0.25 package="0603 [SMD]"]
  C2 = Ceramic Capacitor [capacitance="100 nF" voltage=35V package="0603 [SMD, multilayer]"]
  J19 = male pin header, 2 pins [form="♂ (male)"]
  J20 = male pin header, 2 pins [form="♂ (male)"]
  J17 = male pin header, 2 pins [form="♂ (male)"]
  J18 = male pin header, 2 pins [form="♂ (male)"]
  J15 = male pin header, 2 pins [form="♂ (male)"]
  C7 = Ceramic Capacitor [capacitance=1µF voltage=35V package="0805 [SMD, multilayer]"]
  C12 = Ceramic Capacitor [capacitance=10µF voltage=35V package="0805 [SMD, multilayer]"]
  R29 = male pin header, 1 pin [form="♂ (male)"]
  J28 = male pin header, 1 pin [form="♂ (male)"]
  U9 = Voltage Regulator - Variable [package="TO220 [THT]"]
  C14 = Ceramic Capacitor [capacitance=10µF voltage=35V package="0805 [SMD, multilayer]"]
  R30 = Resistor [tolerance=±5% resistance=10k power=0.25 package="0603 [SMD]"]
  R31 = Resistor [tolerance=±5% resistance=10k power=0.25 package="0603 [SMD]"]
  D13 = Rectifier Diode [part_number=1N007 package="300 mil [THT]"]
  C15 = Ceramic Capacitor [capacitance="100 nF" voltage=35V package="0603 [SMD, multilayer]"]
  C16 = Ceramic Capacitor [capacitance="100 nF" voltage=35V package="0603 [SMD, multilayer]"]
  C17 = Ceramic Capacitor [capacitance="100 nF" voltage=35V package="0603 [SMD, multilayer]"]
  C18 = Ceramic Capacitor [capacitance="100 nF" voltage=35V package="0603 [SMD, multilayer]"]
  U10 = SN74LVC1G18DBVR [package=sot-23-6]
  U11 = SN74LVC1G18DBVR [package=sot-23-6]
  U12 = SN74LVC1G18DBVR [package=sot-23-6]
  U13 = SN74LVC1G18DBVR [package=sot-23-6]

nets:
  N1: A1.D1/TX, J26.pin1
  GND: A1.GND, C1.-, Q1.source, U3.0V, U4.0V, U1.pin12, U1.pin27, J5.pin2, J3.pin1, J3.pin2, J3.pin3, J21.pin3, J22.pin3, J23.pin3, J24.pin3, J25.pin3, J26.pin3, J27.pin16, J1.pin2, U7.GND, Q2.source, Q3.source, R24.Pin_0, R18.Pin_0, R19.Pin_0, R20.Pin_0, R10.Pin_1, R12.Pin_1, R11.Pin_1, R9.Pin_1, C6.1, C3.0, C4.1, R15.Pin_0, R4.Pin_1, R5.Pin_1, R7.Pin_1, R13.Pin_0, R14.Pin_0, C9.0, C8.0, U8.GND, C13.1, U5.GND, C11.1, R27.Pin_0, R26.Pin_0, C2.1, C7.1, C12.1, U9.GND, C14.1, R30.Pin_1, R31.Pin_0, C15.0, C16.0, C17.1, C18.1
  N2: A1.D2, U1.pin17
  N3: A1.D3, U1.pin16
  N4: A1.D4, U1.pin15
  N5: A1.D5, U1.pin14
  N6: A1.D6, U1.pin28
  N7: A1.D7, U13.A
  N8: A1.D8, U12.A
  N9: A1.D9, U11.A
  N10: A1.D10, U10.A
  N11: A1.D11/MOSI, U10.S, U11.S, U12.S, U13.S
  N12: A1.D12/MISO, J11.pin4, J27.pin5
  VIN: A1.VIN, J6.pin5, J12.pin2, J12.pin5, JP1.pin2, J7.pin2, J7.pin5, C1.+, J11.pin1, U3.COM_-_Common, U4.COM_-_Common, P2.A, P3.A, P1.A, U1.pin1, U1.pin18, J5.pin1, J2.pin1, J2.pin2, J2.pin3, J14.pin1, J13.pin1, J21.pin2, J22.pin2, J23.pin2, J24.pin2, J25.pin2, J26.pin2, J27.pin2, D6.anode, RL1.pin8, D5.anode, C6.0, C3.1, C4.0, C9.1, C8.1, U8.VCC, C13.0, U5.+V, C11.0, C2.0, J17.pin1, J18.pin1, J15.pin2, C7.0, U9.OUT, C14.0, R30.Pin_0, D13.cathode
  N13: A1.A7, R8.Pin_0
  N14: A1.A5, J5.pin4
  N15: A1.A4, J5.pin3
  N16: A1.A2, P3.S
  N17: A1.A1, P2.S
  N18: A1.A0, P1.S
  N19: A1.3V3, J4.pin1, J4.pin2, J4.pin3
  N20: A1.D13/SCK, J11.pin3, J27.pin6
  N21: J6.pin1, J6.pin3, U7.IN, J8.pin2, J9.pin2, U9.IN
  N22: J6.pin2, D12.cathode
  N23: J6.pin6, U1.pin4, J27.pin14, R15.Pin_1
  N24: J12.pin1, J12.pin6, JP1.pin1, U1.pin11, J27.pin11, R13.Pin_1
  N25: J12.pin3, J12.pin4, JP1.pin3, U1.pin10, J27.pin10, R14.Pin_1
  N26: J7.pin1, J7.pin3, J27.pin7, D7.anode
  N27: J7.pin6, D9.anode
  N28: J11.pin5, R4.Pin_0
  N29: J11.pin6, R5.Pin_0
  N30: J11.pin8, R7.Pin_0
  N31: D1.cathode, J16.pin1, U7.OUT, C12.0, R31.Pin_1
  N32: D1.anode, Q1.drain, J16.pin2
  N33: Q1.gate, R8.Pin_1
  N34: U3.In_1, U10.Y1
  N35: U3.In_2, U11.Y1
  N36: U3.In_3, U12.Y1
  N37: U3.In_4, U13.Y1
  N38: U3.Out_4, J13.pin5
  N39: U3.Out_3, J13.pin4
  N40: U3.Out_2, J13.pin3
  N41: U3.Out_1, J13.pin2
  N42: U4.In_1, U10.Y0
  N43: U4.In_2, U11.Y0
  N44: U4.In_3, U12.Y0
  N45: U4.In_4, U13.Y0
  N46: U4.Out_4, J14.pin5
  N47: U4.Out_3, J14.pin4
  N48: U4.Out_2, J14.pin3
  N49: U4.Out_1, J14.pin2
  N50: P2.E, R19.Pin_1
  N51: P3.E, R18.Pin_1
  N52: P1.E, R20.Pin_1
  N53: U1.pin6, R24.Pin_1, J15.pin1
  N54: U1.pin9, J25.pin1
  N55: U1.pin19, R9.Pin_0, J17.pin2
  N56: U1.pin20, R10.Pin_0, J18.pin2
  N57: U1.pin21, D4.cathode, R11.Pin_0, J19.pin2
  N58: U1.pin22, D3.cathode, R12.Pin_0, J20.pin2
  N59: U1.pin23, J21.pin1
  N60: U1.pin24, J22.pin1
  N61: U1.pin25, J23.pin1
  N62: U1.pin26, J24.pin1, J27.pin1, U5.IN
  N63: J27.pin3, D3.anode
  N64: J27.pin4, D4.anode
  N65: J27.pin8, D10.anode
  N66: J27.pin9, D8.anode
  N67: D6.cathode, J20.pin1
  N68: J1.pin1, D12.anode
  N69: Q2.gate, R23.Pin_1
  N70: Q2.drain, J10.pin5, D2.anode
  N71: J10.pin2, J10.pin3
  N72: J10.pin4, RL1.pin7, D2.cathode
  N73: J8.pin1, J28.pin1
  N74: J8.pin3, R26.Pin_1
  N75: J9.pin1, RL1.pin6
  N76: J9.pin3, R27.Pin_1
  N77: RL1.pin1, Q3.drain, D13.anode
  N78: RL1.pin5, R29.pin1
  N79: Q3.gate, R28.Pin_1
  N80: D9.cathode, D10.cathode, R28.Pin_0
  N81: D7.cathode, D8.cathode, U8.B
  N82: D5.cathode, J19.pin1
  N83: R23.Pin_0, U8.Y
  N84: U8.A, U5.OUT
  VDD: C15.1, C16.1, C17.0, C18.0, U10.VDD, U11.VDD, U12.VDD, U13.VDD
  GND_2: U10.GND, U11.GND, U12.GND, U13.GND

notes:
  Power SW
  Speed SW
  Size SW
  Size Jumper
  12" Play Sensor
  LEDs
  PW SW
  SZ SW
  7-Seg Disp.
  Solenoid
  7S DISP
  SOl
  7"
  12"
  NC = 10"
  Vertical Motor
  Horiz. Motor
  [
  Upper Limit
  Lower Limit
  V MTR
  H MTR
  Pause Button
  Play/Home Button
  U LIM
  L LIM
  PA BT
  PL BT
  7" Play Sensor
  10" Play Sensor
  Home Sensor
  10"
  HOME
  Pickup Sensor
  Speed Sensor
  5v DC
  3.3v DC
  GND
  SPEED
  PICKUP
  7" Cal Pot
  10" Cal Pot
  12" Cal Pot
  33-RPM Pot
  45-RPM Pot
  33 POT
  45 POT
  TURN MTR
  SPD SW
  7" CAL
  10" CAL
  12" CAL
  Automatic Changer Comm
  _
  +5v
  Mux S16
  Mux S15
  Auto-mode indicator (Mux S12)
  5v DC in
  5v DC out
  NC
  Turntable power indicator LED
  33-RPM pot
  J12 pin 2
  45-RPM pot
  J12 pin 3
  J12 pin 4
  Q3 drain
  J10 pin 5
  Power indicator LED (5v)
  Turntable power indicator LED (J10 pin 3)
  Pause status LED (Ard. D13)
  Play status LED (Ard. D12)
  Play status LED GND
  Pause status LED GND
  Turntable power indicator LED GND
  Power indicator LED GND
  SW 1
  SW 2
  SW 3
  SW 4
  SW 5
  SW 6
  5v OUT
  GND OUT
  HOME ST OUT
  AUT ST O
  PAUSE CMD IN
  PLAY CMD IN
  MOVE ST OUT
  PAUSE ST OUT
  SPEED SW ST OUT
  Automatic Record Player v0.2 (March 2022)
  Designed by Patrick Nelson (github.com/pdnelson)
  Calibration Display Button
  CAL
  12v DC in
  Turn Motor
  SPEED SET IN
  TRN PW I
  12v DC
  -
  +
  25-ohm, 5w resistor
  [  ]
  SIZE 1 O
  SIZE 2 O
  Solenoid 5v circuit
  Main 5v circuit
  ]

custom parts:
  Voltage Regulator - Variable: Variable DC Voltage Regulator
  DPDT Relay: DIP DPDT Relay (Double Pole Double Throw)
